# Fritzing sketch FritzingFinal (saved by Fritzing 0.9.4)
breadboards: 1

parts:
  Composant1 = Arduino Uno (Rev3)
  DHT20 = DHT22 Humidity and Temperature Sensor
  C2 = Capacitor [package=cap-pth-small2]
  R2 = Resistor [tolerance=±5% resistance=391 package="0603 [SMD]"]
  Capteur_d'humidité_du_sol = Soil Moisture Sensor
  Relais = 2 channel relay module [package=THT]
  Servo = Basic Servo
  LED = LED - 5mm [color="Red (633nm)" package="5 mm [THT]"]
  R3 = Resistor [tolerance=±5% resistance=220 package="1206 [SMD]"]
  Capteur_de_lumière = Grove Light Sensor
  Atomiseur = seeed grove atomizer v1.0
  Pompe_Peristaltique = water pump/motor
  Mosfet = IFR520 MOS module [package=THT]
  Régulateur_de_tension_DC-DC = Régulateur de tension DC-DC - Module d'alimentation abaisseur réglable avec écran
  Chauffage_résistif = Resistor [tolerance=±5% resistance=10 package="2010 [SMD]"]
  Nextion = Nextion SPI 2.4" LCD NX3224T024_011
  Baterie = Battery Holders [package=lipo-1100mAh]

nets:
  N1: Composant1.A0, R3.Pin_1
  N2: Composant1.A1, Capteur_de_lumière.SIG
  N3: Composant1.A2, Capteur_d'humidité_du_sol.SIG
  N4: Composant1.D8, Relais.pin_15
  N5: Composant1.D9_PWM, Servo.pulse
  N6: Composant1.A4/SDA, DHT20.DATA
  N7: Composant1.A5/SCL, DHT20.GND
  N8: Composant1.D0/RX, Nextion.pin2
  N9: Composant1.D1/TX, Nextion.pin3
  N10: Composant1.D5_PWM, Atomiseur.VCC
  N11: Composant1.D7, Mosfet.SIG
  VCC: Composant1.VIN, R2.Pin_0, Capteur_d'humidité_du_sol.VCC, Relais.pin_1, Relais.pin_13, Capteur_de_lumière.VCC, Mosfet.VCC, Régulateur_de_tension_DC-DC.OUT+, Nextion.VCC
  N12: DHT20.VDD, C2.1, R2.Pin_1
  GND: DHT20.NULL, C2.2, Capteur_d'humidité_du_sol.GND, Relais.pin_14, Servo.gnd, LED.anode, Capteur_de_lumière.GND, Atomiseur.GND, Pompe_Peristaltique.pin_1, Mosfet.GND, Régulateur_de_tension_DC-DC.OUT-, Nextion.GND
  N13: Relais.pin_3, Servo.vcc
  N14: Relais.pin_4, Régulateur_de_tension_DC-DC.IN+, Régulateur_de_tension_DC-DC.IN-, Baterie.+, Baterie.-
  N15: Relais.pin_6, Pompe_Peristaltique.pin_2
  N16: LED.cathode, R3.Pin_0
  N17: Mosfet.V+, Chauffage_résistif.Pin_0
  N18: Mosfet.V-, Chauffage_résistif.Pin_1

custom parts:
  2 channel relay module: 2 channel Relay Module 5V 12V 24V High and Low Level Trigger Relay Control With Optocoupler Two Way relays DC 5 V 12 V 24 V Volt.
  seeed grove atomizer v1.0: Grove - Water Atomization is a perfect module for you to quickly DIY a humidifier with Arduino. You can also develop more advanced and interesting projects with digital scent technology and any other situations in which atomization required.
  water pump/motor: WATER PUMP BY ARDUBLOCKTR
  Régulateur de tension DC-DC - Module d'alimentation abaisseur réglable avec écran: Dollatek - Régulateur de tension DC-DC - Module d'alimentation abaisseur réglable avec écran Avec le voltmètre affiche une erreur de mesure ± 0,1 V, la plage 0-40 V. Touchez la touche pour changer de tension d'entrée ou de sortie, et affiche une lumière qui est mesurée les tensions. Fonction de mémoire de mise hors tension, montre la route après les valeurs de tension mesurées pour la dernière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
