# Fritzing sketch light-sensor (saved by Fritzing 0.9.2b)
breadboards: 1

parts:
  Part1 = Arduino Uno (Rev3)
  Grove1 = Grove Light Sensor
  R1 = Resistor [tolerance=±5% resistance=20k package="0805 [SMD]"]

nets:
  N1: Part1.A0, Grove1.SIG
  GND: Part1.GND, Grove1.GND
  N2: Grove1.VCC, R1.Pin_0

notes:
  STEP 1
  Attach your 5v (red) wire to the rail of the breadboard
  Attach your GND (black) wire to the rail of the breadboard
  The light sensor has 3 leads coming out of it
  GND (ground) attach black wire
  VCC (voltage) attach red wire
  S (signal) attach yellow wire
  use a 20k resistor

custom parts:
  Grove Light Sensor: An analog light sensor
